# Fritzing sketch final (saved by Fritzing 0.9.3b)
breadboards: 1

parts:
  Composant1 = Arduino Uno (Rev3)
  R1 = Resistor [tolerance=±5% resistance=10 package=THT]
  C1 = Ceramic Capacitor [capacitance=100nF package="100 mil [THT, multilayer]"]
  R2 = Resistor [tolerance=±5% resistance=1M package=THT]
  R3 = Resistor [tolerance=±5% resistance=220 package=THT]
  LED1 = LED - 5mm [color="Red (633nm)" package="5 mm [THT]"]
  R4 = Resistor [tolerance=±5% resistance=220 package=THT]
  LED2 = LED - 5mm [color="Yellow (595nm)" package="5 mm [THT]"]
  R5 = Resistor [tolerance=±5% resistance=220 package=THT]
  LED3 = LED - 5mm [color="Green (570nm)" package="5 mm [THT]"]

nets:
  N1: Composant1.A0, C1.1, R2.Pin_0
  N2: Composant1.D9_PWM, R1.Pin_0
  N3: Composant1.GND, R2.Pin_1, LED1.anode, LED2.anode, LED3.anode
  N4: Composant1.D4, R3.Pin_0
  N5: Composant1.D5_PWM, R4.Pin_0
  N6: Composant1.D6_PWM, R5.Pin_0
  N7: R1.Pin_1, C1.0
  N8: R3.Pin_1, LED1.cathode
  N9: R4.Pin_1, LED2.cathode
  N10: R5.Pin_1, LED3.cathode
